// Logisim project scheme.circ as structural Verilog
module Arithmetic_Logic_Unit (
);

  wire adcsbb_1_p2, adcsbb_1_p4, adcsbb_1_p5, and_1_p1, and_1_p2, and_2_out, and_3_out, rightshift_1_p1,
       rightshift_1_p2;
  wire [3:0] or_2_out;

  // And and_1: pin names not known; wires that end beside it: and_1_p1, and_1_p2
  // Or or_1: pin names not known
  // Nor nor_1: pin names not known
  // RightShift rightshift_1: pin names not known; wires that end beside it: rightshift_1_p1, rightshift_1_p2
  and and_2 (and_2_out, rightshift_1_p2, rightshift_1_p1);
  // AdcSbb adcsbb_1: pin names not known; wires that end beside it: rightshift_1_p1, adcsbb_1_p2, and_1_p2, adcsbb_1_p4, adcsbb_1_p5
  and and_3 (and_3_out, adcsbb_1_p5, adcsbb_1_p2);
  // Comparator comparator_1: pin names not known; wires that end beside it: adcsbb_1_p2, or_2_out[1], or_2_out[2], or_2_out[3]
  or or_2 (or_2_out[0], and_2_out, and_3_out);
endmodule
